# Fritzing sketch Exercise three (saved by Fritzing 0.9.0b)
breadboards: 1

parts:
  LED1 = LED - 5mm [color="Red (633nm)" package="5 mm [THT]"]
  Part1 = Arduino Uno (Rev3)
  LED2 = LED - 5mm [color="White (6500K)" package="5 mm [THT]"]
  LED3 = LED - 5mm [color="Blue (470nm)" package="5 mm [THT]"]
  R2 = Resistor [tolerance=±5% resistance=220 package=THT]
  R3 = Resistor [tolerance=±5% resistance=220 package=THT]
  R4 = Resistor [tolerance=±5% resistance=220 package=THT]

nets:
  N1: LED1.cathode, Part1.GND, LED2.cathode, LED3.cathode
  N2: LED1.anode, R2.Pin_0
  N3: Part1.D11_PWM/MOSI, R3.Pin_1
  N4: Part1.D12/MISO, R4.Pin_1
  N5: Part1.D13/SCK, R2.Pin_1
  N6: LED2.anode, R4.Pin_0
  N7: LED3.anode, R3.Pin_0
