# Fritzing sketch Exercise 4 (saved by Fritzing 0.9.0b)
breadboards: 1

parts:
  LED1 = LED - 5mm [color="Red (633nm)" package="5 mm [THT]"]
  R1 = Resistor [tolerance=±5% resistance=220 package=THT]
  Part1 = Arduino Uno (Rev3)
  R2 = Rotary Potentiometer (Small) [maximum_resistance=100kΩ package=THT]

nets:
  N1: LED1.cathode, Part1.GND, R2.leg1
  N2: LED1.anode, R1.Pin_0
  N3: R1.Pin_1, R2.wiper
  N4: Part1.D13/SCK, R2.leg2
