# Fritzing sketch Exercise two (saved by Fritzing 0.9.0b)
breadboards: 1

parts:
  LED1 = LED - 5mm [color="Red (633nm)" package="5 mm [THT]"]
  R1 = Resistor [tolerance=±5% resistance=220 package=THT]
  Part1 = Arduino Uno (Rev3)
  LED2 = LED - 5mm [color="White (6500K)" package="5 mm [THT]"]
  R2 = Resistor [tolerance=±5% resistance=220 package=THT]
  R3 = Resistor [tolerance=±5% resistance=220 package=THT]
  LED3 = LED - 5mm [color="Blue (470nm)" package="5 mm [THT]"]

nets:
  N1: LED1.cathode, R1.Pin_1, Part1.GND, LED2.cathode, R3.Pin_1, LED3.cathode
  N2: LED1.anode, R2.Pin_0
  N3: R1.Pin_0, LED2.anode
  N4: Part1.D13/SCK, R2.Pin_1
  N5: R3.Pin_0, LED3.anode
