# Fritzing sketch Exercise 6 (saved by Fritzing 0.9.0b)
breadboards: 1

parts:
  Part1 = Arduino Uno (Rev3)
  R1 = Rotary Potentiometer (Small) [maximum_resistance=100kΩ package=THT]
  R2 = Rotary Potentiometer (Small) [maximum_resistance=100kΩ package=THT]

nets:
  N1: Part1.A0, R2.wiper
  N2: Part1.A2, R1.wiper
  N3: Part1.5V, R1.leg2, R2.leg2
  N4: Part1.GND, R1.leg1, R2.leg1
