# Fritzing sketch Exercise 7 (saved by Fritzing 0.9.0b)
breadboards: 1

parts:
  Part1 = Arduino Uno (Rev3)
  J1 = Basic Servo
  R1 = Rotary Potentiometer (Small) [maximum_resistance=10kΩ package=THT]

nets:
  N1: Part1.A0, R1.wiper
  N2: Part1.D8, J1.pulse
  5V: Part1.5V, J1.vcc, R1.leg2
  GND: Part1.GND, J1.gnd, R1.leg1
