# Fritzing sketch Exercise 11 (saved by Fritzing 0.9.0b)
breadboards: 1

parts:
  Part1 = Arduino Uno (Rev3)
  R1 = Rotary Potentiometer (Small) [maximum_resistance=10kΩ package=THT]
  M1 = DC Motor

nets:
  N1: Part1.A0, R1.wiper
  N2: Part1.D3_PWM, M1.pin_2
  N3: Part1.5V, R1.leg2
  N4: Part1.GND, R1.leg1, M1.pin_1
