# Fritzing sketch Exercise_16 (saved by Fritzing 0.9.0b)
breadboards: 1

parts:
  Part1 = Arduino Uno (Rev3)
  J1 = Piezo Speaker
  R1 = Resistor [tolerance=±5% resistance=1k package=THT]
  R2 = Photocell (LDR) [package=THT]

nets:
  N1: Part1.A0, R1.Pin_1, R2.pin_0
  N2: Part1.D12/MISO, J1.pin1
  N3: Part1.GND, J1.pin2, R1.Pin_0
  N4: Part1.5V, R2.pin_1
